# Fritzing sketch potentiometer-motor (saved by Fritzing 0.9.2b)
breadboards: 1

parts:
  Part1 = Arduino Uno (Rev3)
  M1 = DC Motor
  D1 = Rectifier Diode [part_number=1N4001 package="300 mil [THT]"]
  R1 = Resistor [tolerance=±5% resistance=330 package=THT]
  Q1 = NPN-Transistor [package="TO92 [THT]"]
  R3 = Resistor [tolerance=±5% resistance=220 package=THT]
  R2 = Slide Potentiometer [maximum_resistance=10kΩ]

nets:
  N1: Part1.A0, R3.Pin_0, R2.wiper
  N2: Part1.D9_PWM, R1.Pin_0
  N3: Part1.GND, Q1.E, R3.Pin_1, R2.leg1
  N4: Part1.5V, M1.pin_1, D1.cathode, R2.leg2
  N5: M1.pin_2, D1.anode, Q1.C
  N6: R1.Pin_1, Q1.B
